# Fritzing sketch schema (saved by Fritzing 1.0.6)
breadboards: 1

parts:
  A1 = Raspberry Pi Pico2
  A2 = Raspberry Pi Pico2

nets:
  N1: A1.pin_1, A2.pin_2
  N2: A1.pin_2, A2.pin_1
  N3: A1.pin_3, A1.pin_8, A1.pin_13, A1.pin_18, A1.pin_23, A1.pin_28, A1.pin_33, A1.pin_38, A2.pin_3, A2.pin_8, A2.pin_13, A2.pin_18, A2.pin_23, A2.pin_28, A2.pin_33, A2.pin_38

custom parts:
  Raspberry Pi Pico2: Raspberry Pi Pico 2W is our new $7 microcontroller board, built on RP2350: our new high-performance, secure microcontroller with on board WiFi.
